// Logisim project ADD-SUBB.circ as structural Verilog: 8 circuits, main circuit Prototype
module A_S_1B (
  input  RIN,
  input  B,
  input  A,
  output R_out,
  output S
);

  wire and_1_out, and_2_out, xor_1_out;

  xor xor_1 (xor_1_out, A, B);
  xor xor_2 (S, xor_1_out, RIN);
  and and_1 (and_1_out, xor_1_out, RIN);
  and and_2 (and_2_out, B, A);
  or or_1 (R_out, and_1_out, and_2_out);
endmodule

module A_S_4B (
  input  A1,
  input  B_1,
  input  A2,
  input  B2,
  input  A3,
  input  B3,
  input  A4,
  input  B4,
  input  RIN,
  output R_out,
  output S3,
  output S2,
  output S1,
  output S0
);

  wire a_s_1b_2_r_out, a_s_1b_3_r_out, a_s_1b_4_r_out;

  A_S_1B a_s_1b_1 (.RIN(A1), .B(B_1), .A(a_s_1b_2_r_out), .R_out(R_out), .S(S3));
  A_S_1B a_s_1b_2 (.RIN(A2), .B(B2), .A(a_s_1b_3_r_out), .R_out(a_s_1b_2_r_out), .S(S2));
  A_S_1B a_s_1b_3 (.RIN(A3), .B(B3), .A(a_s_1b_4_r_out), .R_out(a_s_1b_3_r_out), .S(S1));
  A_S_1B a_s_1b_4 (.RIN(A4), .B(B4), .A(RIN), .R_out(a_s_1b_4_r_out), .S(S0));
endmodule

module Prototype (
  input  B1,
  input  B2,
  input  B3,
  input  B_4,
  input  in_5,
  input  A1,
  input  A2,
  input  A3,
  input  A4,
  output out_10,
  output out_11,
  output out_12,
  output out_13,
  output out_14
);

  wire xor_1_out, xor_2_out, xor_3_out, xor_4_out;

  xor xor_1 (xor_1_out, in_5, B1);
  xor xor_2 (xor_2_out, in_5, B3);
  xor xor_3 (xor_3_out, in_5, B2);
  xor xor_4 (xor_4_out, in_5, B_4);
  A_S_4B a_s_4b_1 (
    .A1(A1), .B_1(xor_1_out), .A2(A2), .B2(xor_3_out), .A3(A3), .B3(xor_2_out), .A4(A4), .B4(xor_4_out),
    .RIN(in_5), .R_out(out_10), .S3(out_11), .S2(out_12), .S1(out_13), .S0(out_14));
endmodule

module OVA1 (
  input  in_1,
  input  in_2,
  input  in_3,
  input  in_4,
  output out_5,
  output out_6,
  output out_7,
  output out_8
);

  wire clock_1_out, clock_2_out, clock_3_out, undriven;

  Clock #(.lowDuration(25)) clock_1 (.out(clock_1_out));
  Clock #(.highDuration(15), .lowDuration(5)) clock_2 (.out(clock_2_out));
  Clock #(.lowDuration(5)) clock_3 (.out(clock_3_out));
  Prototype prototype_1 (
    .in_5(1'b0), .B1(clock_1_out), .B2(undriven), .B3(clock_2_out), .B_4(clock_3_out), .A1(in_1), .A2(in_2),
    .A3(in_3), .A4(in_4), .out_11(out_8), .out_12(out_7), .out_13(out_6), .out_14(out_5));  // open: out_10
  // AND_Gate and_1 is placed but not wired
endmodule

module OKL (
  output out_1,
  output out_2,
  output out_3,
  output out_4
);

  wire deco_1_x1, deco_1_x2, deco_1_x3, deco_1_x4, deco_1_x5, deco_1_x6, deco_1_x7;

  Clock #(.highDuration(48), .lowDuration(48)) clock_1 (.out(out_1));
  Clock #(.highDuration(24), .lowDuration(24)) clock_2 (.out(out_2));
  Clock #(.highDuration(12), .lowDuration(12)) clock_3 (.out(out_3));
  Clock #(.highDuration(6), .lowDuration(6)) clock_4 (.out(out_4));
  DECO deco_1 (
    .i0(out_1), .i1(out_2), .i2(out_3), .i3(out_4), .x1(deco_1_x1), .x2(deco_1_x2), .x3(deco_1_x3),
    .x4(deco_1_x4), .x5(deco_1_x5), .x6(deco_1_x6), .x7(deco_1_x7));
  _7_Segment_Display u_7_segment_display_1 (
    .g(deco_1_x4), .f(deco_1_x3), .a(deco_1_x2), .b(deco_1_x1), .e(deco_1_x5), .d(deco_1_x6), .c(deco_1_x7));  // open: dp
endmodule

module DECO (
  input  i0,
  input  i1,
  input  i2,
  input  i3,
  output x1,
  output x2,
  output x3,
  output x4,
  output x5,
  output x6,
  output x7
);

  wire and_1_out, and_2_out, and_3_out, and_4_out, and_5_out, and_6_out, and_7_out, and_8_out, and_9_out,
       and_10_out, and_11_out, and_12_out, and_13_out, and_14_out, and_15_out, and_16_out, and_17_out,
       and_18_out, and_19_out, and_20_out, and_21_out, and_22_out, and_23_out, and_24_out, and_25_out,
       and_26_out, and_27_out, and_28_out, and_29_out, and_30_out, and_31_out, not_1_out, not_2_out,
       not_3_out, not_4_out, not_5_out, not_6_out, not_7_out, not_8_out, not_9_out, not_10_out, not_11_out,
       not_12_out, not_13_out, not_14_out, not_15_out, not_16_out, not_17_out, not_18_out, not_19_out,
       not_20_out, not_21_out, not_22_out, not_23_out, not_24_out, not_25_out, not_26_out, not_27_out,
       not_28_out, not_29_out, not_30_out, not_31_out, not_32_out, not_33_out, not_34_out, not_35_out,
       not_36_out, not_37_out, not_38_out, not_39_out, not_40_out, not_41_out, not_42_out, not_43_out;

  not not_1 (not_1_out, i1);
  not not_2 (not_2_out, i2);
  and and_1 (and_1_out, not_2_out, not_3_out);
  not not_3 (not_3_out, i3);
  not not_4 (not_4_out, i0);
  and and_2 (and_2_out, not_4_out, i2, i3);
  and and_3 (and_3_out, i0, not_5_out);
  not not_5 (not_5_out, i2);
  and and_4 (and_4_out, i0, not_6_out);
  not not_6 (not_6_out, i3);
  not not_7 (not_7_out, i1);
  and and_5 (and_5_out, not_7_out, not_8_out);
  not not_8 (not_8_out, i3);
  not not_9 (not_9_out, i0);
  and and_6 (and_6_out, not_9_out, i2);
  and and_7 (and_7_out, i1, i3);
  and and_8 (and_8_out, i0, not_10_out);
  not not_10 (not_10_out, i2);
  not not_11 (not_11_out, i0);
  and and_9 (and_9_out, not_11_out, not_12_out, not_13_out);
  not not_12 (not_12_out, i2);
  not not_13 (not_13_out, i3);
  not not_14 (not_14_out, i0);
  and and_10 (and_10_out, not_14_out, i1, not_15_out);
  not not_15 (not_15_out, i2);
  not not_16 (not_16_out, i0);
  and and_11 (and_11_out, not_16_out, i1, not_17_out);
  not not_17 (not_17_out, i3);
  and and_12 (and_12_out, i0, not_18_out, not_19_out);
  not not_18 (not_18_out, i1);
  not not_19 (not_19_out, i2);
  and and_13 (and_13_out, i0, not_20_out, not_21_out);
  not not_20 (not_20_out, i1);
  not not_21 (not_21_out, i3);
  and and_14 (and_14_out, i0, i1, i2);
  not not_22 (not_22_out, i0);
  and and_15 (and_15_out, not_22_out, not_23_out, i2);
  not not_23 (not_23_out, i1);
  and and_16 (and_16_out, i1, not_24_out);
  not not_24 (not_24_out, i2);
  and and_17 (and_17_out, i1, not_25_out);
  not not_25 (not_25_out, i3);
  and and_18 (and_18_out, i0, not_26_out);
  not not_26 (not_26_out, i2);
  and and_19 (and_19_out, i0, i1);
  not not_27 (not_27_out, i1);
  and and_20 (and_20_out, not_27_out, not_28_out);
  not not_28 (not_28_out, i3);
  not not_29 (not_29_out, i0);
  and and_21 (and_21_out, not_29_out, i2, not_30_out);
  not not_30 (not_30_out, i3);
  and and_22 (and_22_out, i0, not_31_out, not_32_out);
  not not_31 (not_31_out, i2);
  not not_32 (not_32_out, i3);
  not not_33 (not_33_out, i1);
  and and_23 (and_23_out, not_33_out, not_34_out);
  not not_34 (not_34_out, i3);
  not not_35 (not_35_out, i0);
  and and_24 (and_24_out, not_35_out, not_36_out, i2);
  not not_36 (not_36_out, i1);
  not not_37 (not_37_out, i0);
  and and_25 (and_25_out, not_37_out, i2, not_38_out);
  not not_38 (not_38_out, i3);
  not not_39 (not_39_out, i2);
  and and_26 (and_26_out, i1, not_39_out, i3);
  and and_27 (and_27_out, i0, not_40_out);
  not not_40 (not_40_out, i2);
  and and_28 (and_28_out, i0, i1, i3);
  not not_41 (not_41_out, i0);
  and and_29 (and_29_out, not_41_out, not_42_out);
  not not_42 (not_42_out, i2);
  and and_30 (and_30_out, i1, i2);
  and and_31 (and_31_out, i0, not_43_out);
  not not_43 (not_43_out, i1);
  or or_1 (x1, not_1_out, and_1_out, and_2_out, and_3_out, and_4_out);
  or or_2 (x2, and_5_out, and_6_out, and_7_out, and_8_out);
  or or_3 (x4, and_15_out, and_16_out, and_17_out, and_18_out, and_19_out);
  or or_4 (x5, and_20_out, and_21_out, and_22_out);
  or or_5 (x7, and_29_out, i3, and_30_out, and_31_out);
  or or_6 (x3, and_9_out, and_10_out, and_11_out, and_12_out, and_13_out, and_14_out);
  or or_7 (x6, and_23_out, and_24_out, and_25_out, and_26_out, and_27_out, and_28_out);
endmodule

module OVA2 (
  output out_1,
  output out_2,
  output out_3,
  output out_4
);

  wire deco_1_x1, deco_1_x2, deco_1_x3, deco_1_x4, deco_1_x5, deco_1_x6, deco_1_x7;

  Clock #(.highDuration(24), .lowDuration(24)) clock_1 (.out(out_2));
  DECO2 deco2_1 ();  // open: i0, i1, i2, i3, s
  Clock #(.highDuration(12), .lowDuration(12)) clock_2 (.out(out_3));
  Clock #(.highDuration(6), .lowDuration(6)) clock_3 (.out(out_4));
  DECO deco_1 (
    .i0(out_1), .i1(out_2), .i2(out_3), .i3(out_4), .x1(deco_1_x1), .x2(deco_1_x2), .x3(deco_1_x3),
    .x4(deco_1_x4), .x5(deco_1_x5), .x6(deco_1_x6), .x7(deco_1_x7));
  _7_Segment_Display u_7_segment_display_1 (
    .g(deco_1_x4), .f(deco_1_x3), .a(deco_1_x2), .b(deco_1_x1), .e(deco_1_x5), .d(deco_1_x6), .c(deco_1_x7));  // open: dp
endmodule

module DECO2 (
  input  i0,
  input  i1,
  input  i2,
  input  i3,
  output s
);

  wire not_1_out, not_2_out;

  not not_1 (not_1_out, i1);
  and and_1 (s, i0, not_1_out, not_2_out);
  not not_2 (not_2_out, i2);
endmodule
