// Logisim project Asyn_Compteur15.circ as structural Verilog: 1 circuit, main circuit main
module main (
  output out_1,
  output out_2,
  output out_3,
  output out_4
);

  wire clock_1_out, j_k_ff_1_q, j_k_ff_2_q, j_k_ff_3_q;

  Clock clock_1 (.out(clock_1_out));
  J_K_Flip_Flop j_k_ff_1 (
    .J(1'b1), .clk(clock_1_out), .K(1'b1), .Q(j_k_ff_1_q), .Qn(out_2));  // open: preset, en, reset
  J_K_Flip_Flop j_k_ff_2 (.J(1'b1), .clk(j_k_ff_1_q), .K(1'b1), .Q(j_k_ff_2_q), .Qn(out_3));  // open: preset, en, reset
  J_K_Flip_Flop j_k_ff_3 (.J(1'b1), .clk(j_k_ff_2_q), .K(1'b1), .Q(j_k_ff_3_q), .Qn(out_4));  // open: preset, en, reset
  J_K_Flip_Flop j_k_ff_4 (.J(1'b1), .clk(j_k_ff_3_q), .K(1'b1), .Qn(out_1));  // open: Q, preset, en, reset
  Hex_Digit_Display hex_digit_display_1 (.value({out_1, out_4, out_3, out_2}));  // open: dp
endmodule
