// Logisim project COMPT_ANNE.circ as structural Verilog
module Y (
  input  V,
  input  [3:0] END,
  output [3:0] S
);

  wire clock_1_out, comparator_1_eq, j_k_ff_1_q, j_k_ff_1_qn, j_k_ff_2_q, j_k_ff_2_qn, j_k_ff_3_q,
       j_k_ff_3_qn, j_k_ff_4_q;

  Clock #(.highDuration(2), .lowDuration(2)) clock_1 (.out(clock_1_out));
  Comparator #(.width(4), .mode("unsigned")) comparator_1 (.a(END), .b(S), .eq(comparator_1_eq));  // open: gt, lt
  J_K_Flip_Flop j_k_ff_1 (
    .J(V), .clk(clock_1_out), .K(V), .Q(j_k_ff_1_q), .Qn(j_k_ff_1_qn), .en(V), .reset(comparator_1_eq));  // open: preset
  J_K_Flip_Flop j_k_ff_2 (
    .J(V), .clk(j_k_ff_1_qn), .K(V), .Q(j_k_ff_2_q), .Qn(j_k_ff_2_qn), .en(V), .reset(comparator_1_eq));  // open: preset
  J_K_Flip_Flop j_k_ff_3 (
    .J(V), .clk(j_k_ff_2_qn), .K(V), .Q(j_k_ff_3_q), .Qn(j_k_ff_3_qn), .en(V), .reset(comparator_1_eq));  // open: preset
  J_K_Flip_Flop j_k_ff_4 (
    .J(V), .clk(j_k_ff_3_qn), .K(V), .Q(j_k_ff_4_q), .en(V), .reset(comparator_1_eq));  // open: Qn, preset
  Hex_Digit_Display hex_digit_display_1 (.value(S));  // open: dp
  rev rev_1 (
    .i0(j_k_ff_1_q), .i1(j_k_ff_2_q), .i2(j_k_ff_3_q), .i3(j_k_ff_4_q), .o1(S[2]), .o2(S[1]), .o3(S[0]),
    .o0(S[3]));
endmodule

module rev (
  input  i0,
  input  i1,
  input  i2,
  input  i3,
  output o0,
  output o1,
  output o2,
  output o3
);


  assign o0 = i3;
  assign o1 = i2;
  assign o2 = i1;
  assign o3 = i0;
endmodule

// 59:59
module JK_UP_MM_SS (
  output [3:0] out_1,
  output [3:0] out_2,
  output [3:0] out_3,
  output [3:0] out_4,
  output out_5
);

  wire and_1_out, and_2_out, and_4_out, comparator_1_eq, comparator_2_eq, comparator_3_eq, comparator_4_eq,
       comparator_5_eq, comparator_6_eq;
  wire [3:0] n0101_1_out_1, n0101_3_out_1, n0110_1_out_1, n0110_2_out_1, n1001_1_out_1, n1001_2_out_1,
       n1001_3_out_1, n1001_4_out_1, n1010_1_out_1, n1010_2_out_1;

  and and_1 (and_1_out, and_4_out, comparator_2_eq);
  _0101 u_0101_1 (.out_1(n0101_1_out_1));
  _1001 u_1001_1 (.out_1(n1001_1_out_1));
  _1001 u_1001_2 (.out_1(n1001_2_out_1));
  Comparator #(.width(4), .mode("unsigned")) comparator_1 (
    .a(out_1), .b(n0101_1_out_1), .eq(comparator_1_eq));  // open: gt, lt
  and and_2 (and_2_out, comparator_1_eq, comparator_3_eq);
  Y y_1 (.V(and_1_out), .S(out_1), .END(n0110_1_out_1));
  _0110 u_0110_1 (.out_1(n0110_1_out_1));
  Comparator #(.width(4), .mode("unsigned")) comparator_2 (
    .a(n1001_1_out_1), .b(out_4), .eq(comparator_2_eq));  // open: gt, lt
  Comparator #(.width(4), .mode("unsigned")) comparator_3 (
    .a(out_4), .b(n1001_2_out_1), .eq(comparator_3_eq));  // open: gt, lt
  _0101 u_0101_2 ();  // open: out_1
  and and_3 (out_5, and_2_out, and_4_out);
  Hex_Digit_Display hex_digit_display_1 (.value(out_4));  // open: dp
  Hex_Digit_Display hex_digit_display_2 (.value(out_1));  // open: dp
  _1001 u_1001_3 (.out_1(n1001_3_out_1));
  _1001 u_1001_4 (.out_1(n1001_4_out_1));
  _1010 u_1010_1 (.out_1(n1010_1_out_1));
  Y y_2 (.V(and_4_out), .S(out_4), .END(n1010_1_out_1));
  and and_4 (and_4_out, comparator_5_eq, comparator_6_eq);
  Comparator #(.width(4), .mode("unsigned")) comparator_4 (
    .a(n1001_3_out_1), .b(out_3), .eq(comparator_4_eq));  // open: gt, lt
  Comparator #(.width(4), .mode("unsigned")) comparator_5 (
    .a(out_3), .b(n1001_4_out_1), .eq(comparator_5_eq));  // open: gt, lt
  _0101 u_0101_3 (.out_1(n0101_3_out_1));
  Hex_Digit_Display hex_digit_display_3 (.value(out_2));  // open: dp
  Y y_3 (.V(comparator_4_eq), .S(out_2), .END(n0110_2_out_1));
  _0110 u_0110_2 (.out_1(n0110_2_out_1));
  Y y_4 (.V(1'b1), .S(out_3), .END(n1010_2_out_1));
  _1010 u_1010_2 (.out_1(n1010_2_out_1));
  Comparator #(.width(4), .mode("unsigned")) comparator_6 (
    .a(out_2), .b(n0101_3_out_1), .eq(comparator_6_eq));  // open: gt, lt
  Hex_Digit_Display hex_digit_display_4 (.value(out_3));  // open: dp

  // Notes on the sheet:
  //   IDENTIFY : MM = 59
  //   IDENTIFY : SS = 59
endmodule

module _1001 (
  output [3:0] out_1
);


  assign out_1 = 4'b1001;
endmodule

module _1010 (
  output [3:0] out_1
);


  assign out_1 = 4'b1010;
endmodule

module _0000 (
  output [3:0] out_1
);


  assign out_1 = 4'b0000;
endmodule

module _0110 (
  output [3:0] out_1
);


  assign out_1 = 4'b0110;
endmodule

module _0101 (
  output [3:0] out_1
);


  assign out_1 = 4'b0101;
endmodule

module JHMS (
  output [3:0] J1,
  output [3:0] J2,
  output [3:0] H1,
  output [3:0] H2,
  output [3:0] M1,
  output [3:0] M2,
  output [3:0] S1,
  output [3:0] S2,
  output K
);

  wire and_1_out, and_3_out, and_4_out, comparator_1_eq, comparator_2_eq, comparator_3_eq, comparator_4_eq,
       comparator_5_eq, jk_up_mm_ss_1_out_5;
  wire [3:0] inc_1_o1, subtractor_1_out;

  and and_1 (and_1_out, comparator_1_eq, and_3_out);
  Y y_1 (.V(and_1_out), .S(J1), .END(4'b0011));
  Comparator #(.width(4)) comparator_1 (.a(4'b1001), .b(J2), .eq(comparator_1_eq));  // open: gt, lt
  Hex_Digit_Display hex_digit_display_1 (.value(J1));  // open: dp
  INC inc_1 (
    .a1(H1[0]), .a2(H1[1]), .a3(H1[2]), .a4(H1[3]), .o1(inc_1_o1[0]), .o2(inc_1_o1[1]), .o3(inc_1_o1[2]),
    .o4(inc_1_o1[3]));
  Y y_2 (.V(and_3_out), .S(J2), .END(4'b1010));
  and and_2 (K, comparator_1_eq, and_3_out, comparator_3_eq);
  Hex_Digit_Display hex_digit_display_2 (.value(J2));  // open: dp
  Y y_3 (.V(and_4_out), .S(H1), .END(4'b0011));
  Comparator #(.width(4)) comparator_2 (.a(H1), .b(4'b0010), .eq(comparator_2_eq));  // open: gt, lt
  Comparator #(.width(4)) comparator_3 (.a(J1), .b(4'b0010), .eq(comparator_3_eq));  // open: gt, lt
  Hex_Digit_Display hex_digit_display_3 (.value(H2));  // open: dp
  Hex_Digit_Display hex_digit_display_4 (.value(H1));  // open: dp
  Y y_4 (.V(jk_up_mm_ss_1_out_5), .S(H2), .END(inc_1_o1));
  and and_3 (and_3_out, comparator_2_eq, comparator_5_eq, jk_up_mm_ss_1_out_5);
  Hex_Digit_Display hex_digit_display_5 (.value(M1));  // open: dp
  Comparator #(.width(4)) comparator_4 (.a(H2), .b(subtractor_1_out), .eq(comparator_4_eq));  // open: gt, lt
  and and_4 (and_4_out, comparator_4_eq, jk_up_mm_ss_1_out_5);
  Comparator #(.width(4)) comparator_5 (.a(H2), .b(subtractor_1_out), .eq(comparator_5_eq));  // open: gt, lt
  Hex_Digit_Display hex_digit_display_6 (.value(M2));  // open: dp
  JK_UP_MM_SS jk_up_mm_ss_1 (.out_4(M2), .out_1(M1), .out_2(S1), .out_3(S2), .out_5(jk_up_mm_ss_1_out_5));
  Hex_Digit_Display hex_digit_display_7 (.value(S1));  // open: dp
  Hex_Digit_Display hex_digit_display_8 (.value(S2));  // open: dp
  Subtractor #(.width(4)) subtractor_1 (.a(inc_1_o1), .b(4'b0001), .out(subtractor_1_out));  // open: bin, bout
endmodule

module _0100 (
  output [3:0] out_1
);


  assign out_1 = 4'b0100;
endmodule

module _0011 (
  output [3:0] out_1
);


  assign out_1 = 4'b0011;
endmodule

module _0010 (
  output [3:0] out_1
);


  assign out_1 = 4'b0010;
endmodule

module INC (
  input  a1,
  input  a2,
  input  a3,
  input  a4,
  output o1,
  output o2,
  output o3,
  output o4
);

  wire nand_1_out, nand_2_out, nand_3_out, nand_4_out, nand_5_out, nand_6_out, nand_7_out, nand_8_out,
       nand_9_out, nand_10_out, nand_11_out, nand_12_out;

  nand nand_1 (nand_1_out, a2, a2);
  nand nand_2 (nand_2_out, a3, a3);
  nand nand_3 (nand_3_out, a4, a4);
  nand nand_4 (nand_4_out, a1, a1);
  nand nand_5 (nand_5_out, a3, a3);
  nand nand_6 (nand_6_out, a4, a4);
  nand nand_7 (nand_7_out, a2, a2);
  nand nand_8 (nand_8_out, a3, a3);
  nand nand_9 (nand_9_out, a4, a4);
  nand nand_10 (nand_10_out, nand_1_out, nand_2_out, nand_3_out);
  nand nand_11 (nand_11_out, nand_4_out, a2, nand_5_out, nand_6_out);
  nand nand_12 (nand_12_out, nand_7_out, nand_8_out, nand_9_out);
  nand nand_13 (o2, nand_10_out, nand_10_out);
  nand nand_14 (o3, nand_11_out, nand_11_out);
  nand nand_15 (o4, nand_12_out, nand_12_out);

  assign o1 = 1'b0;
endmodule

module _0001 (
  output [3:0] out_1
);


  assign out_1 = 4'b0001;
endmodule

module MOIS (
  output [3:0] out_1,
  output [3:0] out_2
);

  wire and_1_out, and_2_out, and_3_out, and_4_out, comparator_1_eq, comparator_2_eq, comparator_3_eq,
       comparator_4_eq, jhms_1_k;
  wire [3:0] inc2_1_s, jhms_1_h1, jhms_1_h2, jhms_1_m1, jhms_1_m2, jhms_1_s1, jhms_1_s2, y_1_s, y_2_s, y_3_s,
       y_4_s, y_5_s;

  Y y_1 (.V(and_1_out), .S(y_1_s), .END(4'b1010));
  Hex_Digit_Display hex_digit_display_1 (.value(y_1_s));  // open: dp
  Y y_2 (.V(and_3_out), .S(y_2_s), .END(4'b1010));
  Comparator #(.width(4), .mode("unsigned")) comparator_1 (
    .a(y_2_s), .b(4'b1001), .eq(comparator_1_eq));  // open: gt, lt
  and and_1 (and_1_out, comparator_1_eq, and_3_out);
  Hex_Digit_Display hex_digit_display_2 (.value(y_2_s));  // open: dp
  Hex_Digit_Display hex_digit_display_3 (.value(y_3_s));  // open: dp
  and and_2 (and_2_out, comparator_3_eq, and_4_out);
  Y y_3 (.V(and_2_out), .S(y_3_s), .END(4'b1010));
  Comparator #(.width(4), .mode("unsigned")) comparator_2 (
    .a(y_3_s), .b(4'b1001), .eq(comparator_2_eq));  // open: gt, lt
  and and_3 (and_3_out, comparator_2_eq, and_2_out);
  Hex_Digit_Display hex_digit_display_4 (.value(y_4_s));  // open: dp
  inc2 inc2_1 (.a1(y_5_s[3]), .a2(y_5_s[2]), .a3(y_5_s[1]), .a4(y_5_s[0]), .S(inc2_1_s));
  Y y_4 (.V(and_4_out), .S(y_4_s), .END(4'b1010));
  Comparator #(.width(4), .mode("unsigned")) comparator_3 (
    .a(y_4_s), .b(4'b1001), .eq(comparator_3_eq));  // open: gt, lt
  Hex_Digit_Display hex_digit_display_5 (.value(y_5_s));  // open: dp
  Hex_Digit_Display hex_digit_display_6 (.value(inc2_1_s));  // open: dp
  Comparator #(.width(4), .mode("unsigned")) comparator_4 (
    .a(y_5_s), .b(4'b1100), .eq(comparator_4_eq));  // open: gt, lt
  and and_4 (and_4_out, comparator_4_eq, jhms_1_k);
  Hex_Digit_Display hex_digit_display_7 (.value(out_1));  // open: dp
  Hex_Digit_Display hex_digit_display_8 (.value(out_2));  // open: dp
  Y y_5 (.V(jhms_1_k), .S(y_5_s), .END(4'b1101));
  Hex_Digit_Display hex_digit_display_9 (.value(jhms_1_h1));  // open: dp
  Hex_Digit_Display hex_digit_display_10 (.value(jhms_1_h2));  // open: dp
  Hex_Digit_Display hex_digit_display_11 (.value(jhms_1_m1));  // open: dp
  JHMS jhms_1 (
    .H1(jhms_1_h1), .K(jhms_1_k), .H2(jhms_1_h2), .M2(jhms_1_m2), .M1(jhms_1_m1), .J2(out_1), .J1(out_2),
    .S1(jhms_1_s1), .S2(jhms_1_s2));
  Hex_Digit_Display hex_digit_display_12 (.value(jhms_1_m2));  // open: dp
  Hex_Digit_Display hex_digit_display_13 (.value(jhms_1_s2));  // open: dp
  Hex_Digit_Display hex_digit_display_14 (.value(jhms_1_s1));  // open: dp

  // Notes on the sheet:
  //   Année
  //   Mois
  //   Jours
  //   Heures
  //   Minutes
  //   Secondes
endmodule

module inc2 (
  input  a1,
  input  a2,
  input  a3,
  input  a4,
  output [3:0] S
);

  wire and_1_out, and_2_out;

  and and_1 (and_1_out, a1, a3);
  and and_2 (and_2_out, a1, a2);
  or or_1 (S[0], and_1_out, and_2_out);

  assign S[3:1] = 3'b000;
endmodule

module KAMILIA (
  input  [6:0] in_1,
  input  [6:0] in_2,
  input  [6:0] in_3,
  input  [6:0] in_4,
  input  [6:0] in_5,
  input  [6:0] in_6,
  input  [6:0] in_7,
  input  [6:0] in_8,
  input  [6:0] in_9,
  input  [6:0] in_10
);

  DotMatrix #(.matrixcols(21)) dotmatrix_1 (
    .col0(in_1), .col1(in_2), .col2(in_3), .col3(in_4), .col4(in_5), .col5(in_6), .col6(in_7), .col7(in_8),
    .col8(in_9), .col9(in_10));  // open: col10, col11, col12, col13, col14, col15, col16, col17, col18, col19, col20
endmodule
