// Logisim project LRU.circ as structural Verilog: 5 circuits, main circuit FINAL1
module main (
  input  S0,
  input  S1,
  input  A0,
  input  B0,
  output S
);

  wire and_1_out, and_2_out, and_3_out, and_4_out, and_5_out, not_1_out, not_2_out, not_3_out, not_4_out,
       not_5_out, not_6_out, not_7_out;

  not not_1 (not_1_out, S0);
  not not_2 (not_2_out, S1);
  not not_3 (not_3_out, A0);
  not not_4 (not_4_out, A0);
  not not_5 (not_5_out, S0);
  not not_6 (not_6_out, B0);
  not not_7 (not_7_out, S1);
  and and_1 (and_1_out, not_1_out, not_2_out, not_3_out);
  and and_2 (and_2_out, S1, not_4_out, B0);
  and and_3 (and_3_out, not_5_out, S1, A0);
  and and_4 (and_4_out, S1, A0, not_6_out);
  and and_5 (and_5_out, S0, not_7_out, A0, B0);
  or or_1 (S, and_1_out, and_2_out, and_3_out, and_4_out, and_5_out);
endmodule

// OP Logique
module LOGIQUE (
  input  B2,
  input  B3,
  input  A0,
  input  A1,
  input  A2,
  input  A3,
  input  B0,
  input  B1,
  input  S0,
  input  S1,
  output out_11,
  output out_12,
  output out_13,
  output out_14
);

  main main_1 (.S0(S0), .S1(S1), .A0(A0), .B0(B0), .S(out_11));
  main main_2 (.S0(S0), .S1(S1), .A0(A1), .B0(B1), .S(out_12));
  main main_3 (.S0(S0), .S1(S1), .A0(A2), .B0(B2), .S(out_13));
  main main_4 (.S0(S0), .S1(S1), .A0(A3), .B0(B3), .S(out_14));
endmodule

module FINAL (
  input  A0,
  input  A1,
  input  A2,
  input  A3,
  input  B0,
  input  B1,
  input  B2,
  input  B3,
  input  S3,
  input  S0,
  input  S1,
  input  S4,
  output Q1,
  output Q2,
  output Q3,
  output Q4
);

  wire logique_1_out_11, logique_1_out_12, logique_1_out_13, logique_1_out_14, prototype_1_out_10,
       prototype_1_out_11, prototype_1_out_12, prototype_1_out_13, prototype_1_out_14;

  LOGIQUE logique_1 (
    .S0(S0), .S1(S1), .A0(A0), .A1(A1), .A2(A2), .A3(A3), .B0(B0), .B1(B1), .B2(B2), .B3(B3),
    .out_11(logique_1_out_11), .out_12(logique_1_out_12), .out_13(logique_1_out_13), .out_14(logique_1_out_14));
  DECODER_LO_ARI decoder_lo_ari_1 (
    .L1(logique_1_out_11), .L2(logique_1_out_12), .L3(logique_1_out_13), .L4(logique_1_out_14),
    .P1(prototype_1_out_10), .P2(prototype_1_out_11), .P3(prototype_1_out_12), .P4(prototype_1_out_13),
    .P5(prototype_1_out_14), .S3(S3), .F1(Q1), .F2(Q2), .F3(Q3), .F4(Q4));
  Prototype prototype_1 (
    .in_5(S4), .B1(B0), .B2(B1), .B3(B2), .B_4(B3), .A1(A0), .A2(A1), .A3(A2), .A4(A3),
    .out_10(prototype_1_out_10), .out_11(prototype_1_out_11), .out_12(prototype_1_out_12),
    .out_13(prototype_1_out_13), .out_14(prototype_1_out_14));
endmodule

// LOG/ART
module DECODER_LO_ARI (
  input  L1,
  input  L2,
  input  L3,
  input  L4,
  input  P1,
  input  P2,
  input  P3,
  input  P4,
  input  P5,
  input  S3,
  output F1,
  output F2,
  output F3,
  output F4
);

  wire and_1_out, and_2_out, and_3_out, and_4_out, and_5_out, and_6_out, and_7_out, and_8_out, not_1_out,
       not_2_out, not_3_out, not_4_out;

  not not_1 (not_1_out, S3);
  not not_2 (not_2_out, S3);
  not not_3 (not_3_out, S3);
  not not_4 (not_4_out, S3);
  and and_1 (and_1_out, not_1_out, L1);
  and and_2 (and_2_out, S3, P2);
  and and_3 (and_3_out, not_2_out, L2);
  and and_4 (and_4_out, S3, P3);
  and and_5 (and_5_out, not_3_out, L3);
  and and_6 (and_6_out, S3, P4);
  and and_7 (and_7_out, not_4_out, L4);
  and and_8 (and_8_out, S3, P5);
  or or_1 (F1, and_1_out, and_2_out);
  or or_2 (F2, and_3_out, and_4_out);
  or or_3 (F3, and_5_out, and_6_out);
  or or_4 (F4, and_7_out, and_8_out);
endmodule

module FINAL1 (
  input  in_1,
  input  A,
  input  in_3,
  input  in_4,
  input  in_5,
  input  B,
  input  in_7,
  input  in_8,
  input  LG_AR,
  input  in_10,
  input  _0_1____A_B,
  input  ADD_SUB,
  output out_13,
  output out_14,
  output out_15,
  output out_16
);

  FINAL final_1 (
    .S3(LG_AR), .S4(ADD_SUB), .S0(_0_1____A_B), .S1(in_10), .A0(in_1), .A1(A), .A2(in_3), .A3(in_4),
    .B0(in_5), .B1(B), .B2(in_7), .B3(in_8), .Q1(out_13), .Q2(out_14), .Q3(out_15), .Q4(out_16));

  // Notes on the sheet:
  //   0 = LOGIQUE
  //   0 = ADD
  //   1 = ARITH
  //   1 = SUBB
  //   [0,0] = C1_A
  //   [1,0] = A & B
  //   [1,1] = A XOR B
endmodule
