// Logisim project Shifter_right.circ as structural Verilog: 1 circuit, main circuit main
module main (
);

  wire clock_1_out, not_1_out, s_r_ff_1_q, s_r_ff_1_qn, s_r_ff_2_q, s_r_ff_2_qn, s_r_ff_3_q, s_r_ff_3_qn,
       xor_1_out, xor_2_out;

  not not_1 (not_1_out, xor_2_out);
  Clock clock_1 (.out(clock_1_out));
  S_R_Flip_Flop s_r_ff_1 (
    .S(xor_2_out), .clk(clock_1_out), .R(not_1_out), .Q(s_r_ff_1_q), .Qn(s_r_ff_1_qn));  // open: preset, reset, en
  S_R_Flip_Flop s_r_ff_2 (
    .S(s_r_ff_1_q), .clk(clock_1_out), .R(s_r_ff_1_qn), .Q(s_r_ff_2_q), .Qn(s_r_ff_2_qn));  // open: preset, reset, en
  S_R_Flip_Flop s_r_ff_3 (
    .S(s_r_ff_2_q), .clk(clock_1_out), .R(s_r_ff_2_qn), .Q(s_r_ff_3_q), .Qn(s_r_ff_3_qn));  // open: preset, reset, en
  S_R_Flip_Flop s_r_ff_4 (.S(s_r_ff_3_q), .clk(clock_1_out), .R(s_r_ff_3_qn));  // open: Q, Qn, preset, reset, en
  xor xor_1 (xor_1_out, s_r_ff_3_q, s_r_ff_2_qn);
  xor xor_2 (xor_2_out, xor_1_out, s_r_ff_1_q);
endmodule
