// Logisim project Synchrone_2-4-6-9.circ as structural Verilog: 1 circuit, main circuit main
module main (
);

  wire and_1_out, clock_1_out, j_k_ff_4_qn;
  wire [3:0] j_k_ff_4_q;

  Clock clock_1 (.out(clock_1_out));
  J_K_Flip_Flop j_k_ff_1 (
    .J(and_1_out), .clk(clock_1_out), .K(1'b1), .Q(j_k_ff_4_q[3]));  // open: Qn, preset, en, reset
  and and_1 (and_1_out, j_k_ff_4_q[2], j_k_ff_4_q[1]);
  J_K_Flip_Flop j_k_ff_2 (.J(1'b1), .clk(clock_1_out), .K(1'b1), .Q(j_k_ff_4_q[1]));  // open: Qn, preset, en, reset
  Hex_Digit_Display hex_digit_display_1 (.value(j_k_ff_4_q));  // open: dp
  J_K_Flip_Flop j_k_ff_3 (
    .J(j_k_ff_4_qn), .clk(clock_1_out), .K(j_k_ff_4_q[1]), .Q(j_k_ff_4_q[2]));  // open: Qn, preset, en, reset
  J_K_Flip_Flop j_k_ff_4 (
    .J(and_1_out), .clk(clock_1_out), .K(1'b1), .Q(j_k_ff_4_q[0]), .Qn(j_k_ff_4_qn));  // open: preset, en, reset
endmodule
