// Logisim project Synchrone_35.circ as structural Verilog: 3 circuits, main circuit main
module main (
  output out_1,
  output out_2,
  output out_3,
  output out_4,
  output out_5,
  output out_6
);

  wire and_1_out, clock_1_out, j_k_ff_1_qn, j_k_ff_2_qn, j_k_ff_3_qn, j_k_ff_4_qn, j_k_ff_5_qn, j_k_ff_6_qn,
       not_1_out, not_2_out, not_3_out, not_4_out;
  wire [3:0] deco2_1_o4, deco_1_o4;

  Clock clock_1 (.out(clock_1_out));
  and and_1 (and_1_out, not_1_out, j_k_ff_2_qn, not_3_out, not_4_out, not_2_out, j_k_ff_6_qn);
  not not_1 (not_1_out, j_k_ff_1_qn);
  not not_2 (not_2_out, j_k_ff_5_qn);
  J_K_Flip_Flop j_k_ff_1 (
    .J(1'b1), .clk(clock_1_out), .K(1'b1), .Q(out_1), .Qn(j_k_ff_1_qn), .reset(and_1_out));  // open: preset, en
  not not_3 (not_3_out, j_k_ff_4_qn);
  not not_4 (not_4_out, j_k_ff_3_qn);
  Hex_Digit_Display hex_digit_display_1 (.value(deco2_1_o4));  // open: dp
  J_K_Flip_Flop j_k_ff_2 (
    .J(1'b1), .clk(out_1), .K(1'b1), .Q(out_2), .Qn(j_k_ff_2_qn), .reset(and_1_out));  // open: preset, en
  deco2 deco2_1 (
    .A1(j_k_ff_6_qn), .A2(j_k_ff_5_qn), .A3(j_k_ff_4_qn), .A4(j_k_ff_3_qn), .A5(j_k_ff_2_qn),
    .A6(j_k_ff_1_qn), .O1(deco2_1_o4[3]), .O2(deco2_1_o4[2]), .O3(deco2_1_o4[1]), .O4(deco2_1_o4[0]));
  J_K_Flip_Flop j_k_ff_3 (
    .J(1'b1), .clk(out_2), .K(1'b1), .Q(out_3), .Qn(j_k_ff_3_qn), .reset(and_1_out));  // open: preset, en
  J_K_Flip_Flop j_k_ff_4 (
    .J(1'b1), .clk(out_3), .K(1'b1), .Q(out_4), .Qn(j_k_ff_4_qn), .reset(and_1_out));  // open: preset, en
  Hex_Digit_Display hex_digit_display_2 (.value(deco_1_o4));  // open: dp
  J_K_Flip_Flop j_k_ff_5 (
    .J(1'b1), .clk(out_4), .K(1'b1), .Q(out_5), .Qn(j_k_ff_5_qn), .reset(and_1_out));  // open: preset, en
  DECO deco_1 (
    .A1(j_k_ff_6_qn), .A2(j_k_ff_5_qn), .A3(j_k_ff_4_qn), .A4(j_k_ff_3_qn), .A5(j_k_ff_2_qn),
    .A6(j_k_ff_1_qn), .O1(deco_1_o4[3]), .O2(deco_1_o4[2]), .O3(deco_1_o4[1]), .O4(deco_1_o4[0]));
  J_K_Flip_Flop j_k_ff_6 (
    .J(1'b1), .clk(out_5), .K(1'b1), .Q(out_6), .Qn(j_k_ff_6_qn), .reset(and_1_out));  // open: preset, en
endmodule

module DECO (
  input  A1,
  input  A2,
  input  A3,
  input  A4,
  input  A5,
  input  A6,
  output O1,
  output O2,
  output O3,
  output O4
);

  wire and_1_out, and_2_out, and_3_out, and_4_out, and_5_out, and_6_out, and_7_out, and_8_out, and_9_out,
       and_10_out, and_11_out, and_12_out, and_13_out, and_14_out, not_1_out, not_2_out, not_3_out,
       not_4_out, not_5_out, not_6_out, not_7_out, not_8_out, not_9_out, not_10_out, not_11_out, not_12_out,
       not_13_out, not_14_out, not_15_out, not_16_out, not_17_out, not_18_out, not_19_out, not_20_out,
       not_21_out, not_22_out, not_23_out;

  not not_1 (not_1_out, A2);
  not not_2 (not_2_out, A4);
  not not_3 (not_3_out, A5);
  not not_4 (not_4_out, A3);
  not not_5 (not_5_out, A4);
  not not_6 (not_6_out, A5);
  not not_7 (not_7_out, A2);
  not not_8 (not_8_out, A3);
  not not_9 (not_9_out, A2);
  not not_10 (not_10_out, A4);
  not not_11 (not_11_out, A5);
  not not_12 (not_12_out, A4);
  not not_13 (not_13_out, A1);
  not not_14 (not_14_out, A2);
  not not_15 (not_15_out, A3);
  not not_16 (not_16_out, A3);
  not not_17 (not_17_out, A2);
  not not_18 (not_18_out, A5);
  not not_19 (not_19_out, A3);
  not not_20 (not_20_out, A4);
  not not_21 (not_21_out, A5);
  not not_22 (not_22_out, A4);
  not not_23 (not_23_out, A5);
  and and_1 (and_1_out, not_1_out, A3, not_2_out, not_3_out);
  and and_2 (and_2_out, A2, not_4_out, not_5_out, A5);
  and and_3 (and_3_out, A2, A3, A4, not_6_out);
  and and_4 (and_4_out, not_7_out, not_8_out, A4);
  and and_5 (and_5_out, not_9_out, A4, A5);
  and and_6 (and_6_out, A2, not_10_out, not_11_out);
  and and_7 (and_7_out, A2, A3, not_12_out);
  and and_8 (and_8_out, A1, A5);
  and and_9 (and_9_out, not_13_out, not_14_out, not_15_out, A5);
  and and_10 (and_10_out, not_16_out, A4, A5);
  and and_11 (and_11_out, not_17_out, A3, A4, not_18_out);
  and and_12 (and_12_out, A2, not_19_out, not_20_out, not_21_out);
  and and_13 (and_13_out, A2, A3, not_22_out, A5);
  and and_14 (and_14_out, A1, not_23_out);
  or or_1 (O1, and_1_out, and_2_out, and_3_out);
  or or_2 (O2, and_4_out, and_5_out, and_6_out, and_7_out, and_8_out);
  or or_3 (O3, and_9_out, and_10_out, and_11_out, and_12_out, and_13_out, and_14_out);

  assign O4 = A6;
endmodule

module deco2 (
  input  A1,
  input  A2,
  input  A3,
  input  A4,
  input  A5,
  input  A6,
  output O1,
  output O2,
  output O3,
  output O4
);

  wire and_1_out, and_2_out, and_3_out, and_4_out, and_5_out, and_6_out, not_1_out, not_2_out, not_3_out,
       not_4_out;

  and and_1 (and_1_out, A2, A4);
  and and_2 (and_2_out, A2, A3);
  not not_1 (not_1_out, A2);
  not not_2 (not_2_out, A2);
  not not_3 (not_3_out, A3);
  not not_4 (not_4_out, A4);
  or or_1 (O3, and_1_out, and_2_out, A1);
  and and_3 (and_3_out, not_1_out, A3, A5);
  and and_4 (and_4_out, not_2_out, A3, A4);
  and and_5 (and_5_out, A3, A4, A5);
  and and_6 (and_6_out, A2, not_3_out, not_4_out);
  or or_2 (O4, and_3_out, and_4_out, and_5_out, and_6_out, A1);

  assign O1 = 1'b0;
  assign O2 = 1'b0;
endmodule
